# Fritzing sketch FourButtons (saved by Fritzing 0.8.3b)
circuit board: 5cm x 3cm
breadboards: 1

parts:
  S1 = Pushbutton [package="[THT]"]
  S2 = Pushbutton [package="[THT]"]
  S3 = Pushbutton [package="[THT]"]
  S4 = Pushbutton [package="[THT]"]
  R1 = Resistor [tolerance=±5% resistance=1 package=THT]
  R2 = Resistor [tolerance=±5% resistance=1 package=THT]
  R3 = Resistor [tolerance=±5% resistance=1 package=THT]
  R4 = Resistor [tolerance=±5% resistance=1 package=THT]
  R5 = Resistor [tolerance=±5% resistance=10k package=THT]
  R6 = Resistor [tolerance=±5% resistance=10k package=THT]
  R7 = Resistor [tolerance=±5% resistance=10k package=THT]
  R8 = Resistor [tolerance=±5% resistance=10k package=THT]
  Part1 = Arduino Esplora (Rev4)

nets:
  N1: S1.Pin_1, S1.Pin_2, R1.Pin_0, R5.Pin_1
  N2: S1.Pin_3, S1.Pin_4, S2.Pin_3, S2.Pin_4, S3.Pin_3, S3.Pin_4, S4.Pin_3, S4.Pin_4, Part1.GND
  N3: S2.Pin_1, S2.Pin_2, R2.Pin_0, R6.Pin_1
  N4: S3.Pin_1, S3.Pin_2, R3.Pin_0, R7.Pin_1
  N5: S4.Pin_1, S4.Pin_2, R4.Pin_0, R8.Pin_1
  N6: R1.Pin_1, Part1.INB
  N7: R2.Pin_1, Part1.INA
  N8: R3.Pin_1, Part1.OUT3
  N9: R4.Pin_1, Part1.OUT2
  N10: R5.Pin_0, R6.Pin_0, R7.Pin_0, R8.Pin_0, Part1.5V
